# Fritzing sketch Pedal-Serie (saved by Fritzing 0.9.9b)
circuit board: 10cm x 6cm
breadboards: 2

parts:
  ESP32_(38_Pines) = ESP32-38PinWide [part_number=ESP32-38PinWide]
  Alabanza = LED - 5mm [color="Yellow (592nm)" current=0.030 package="5 mm [THT]"]
  Adoración = LED - 5mm [color="Blue (505nm)" current=0.030 package="5 mm [THT]"]
  Propias = LED - 5mm [color="Red (633nm)" current=0.030 package="5 mm [THT]"]
  Click = LED - 5mm [color="Orange (612nm)" current=0.030 package="5 mm [THT]"]
  R1 = Resistor [tolerance=±10% power=0.25 resistance=330 package=THT]
  R2 = Resistor [tolerance=±10% power=0.25 resistance=330 package=THT]
  R3 = Resistor [tolerance=±10% power=0.25 resistance=330 package=THT]
  R4 = Resistor [tolerance=±10% power=0.25 resistance=330 package=THT]
  Iterador = Pushbutton [package="[THT]"]
  Menos = Pushbutton [package="[THT]"]
  Más = Pushbutton [package="[THT]"]
  Play/Pause = Pushbutton [package="[THT]"]
  Lanzar/Detener_Clips = Pushbutton [package="[THT]"]
  R5 = Resistor [tolerance=±5% power=0.25 resistance=220 package=THT]
  R6 = Resistor [tolerance=±5% power=0.25 resistance=220 package=THT]
  R7 = Resistor [tolerance=±5% power=0.25 resistance=220 package=THT]
  R8 = Resistor [tolerance=±5% power=0.25 resistance=220 package=THT]
  R9 = Resistor [tolerance=±5% power=0.25 resistance=220 package=THT]

nets:
  N1: ESP32_(38_Pines).3.3, Iterador.Pin_1, Iterador.Pin_2, Menos.Pin_1, Menos.Pin_2, Más.Pin_1, Más.Pin_2, Play/Pause.Pin_1, Play/Pause.Pin_2, Lanzar/Detener_Clips.Pin_1, Lanzar/Detener_Clips.Pin_2
  N2: ESP32_(38_Pines).GND, Alabanza.cathode, Adoración.cathode, Propias.cathode, Click.cathode, R5.Pin_1, R6.Pin_1, R7.Pin_1, R8.Pin_1, R9.Pin_1
  N3: ESP32_(38_Pines).GPIO2, R1.Pin_0
  N4: ESP32_(38_Pines).GPIO4, R2.Pin_0
  N5: ESP32_(38_Pines).GPIO17, R3.Pin_0
  N6: ESP32_(38_Pines).GPIO18, R4.Pin_0
  N7: Alabanza.anode, R1.Pin_1
  N8: Adoración.anode, R2.Pin_1
  N9: Propias.anode, R3.Pin_1
  N10: Click.anode, R4.Pin_1
  N11: Iterador.Pin_3, Iterador.Pin_4, R5.Pin_0
  N12: Menos.Pin_3, Menos.Pin_4, R6.Pin_0
  N13: Más.Pin_3, Más.Pin_4, R7.Pin_0
  N14: Play/Pause.Pin_3, Play/Pause.Pin_4, R8.Pin_0
  N15: Lanzar/Detener_Clips.Pin_3, Lanzar/Detener_Clips.Pin_4, R9.Pin_0

custom parts:
  ESP32-38PinWide: Generic 38-Pin ESP32 with wide format (only access to one side of pins on a breadboard) based on Stephen Lilley's HiLetgo ESP-WROOM-32 ESP32 ESP-32S Development Board.
